// Logisim project DesignVorschlag1.circ as structural Verilog: 5 circuits, main circuit main
module main (
);

  wire [15:0] regfile_1_operand1, regfile_1_operand2;

  RegFile regfile_1 (
    .Operand1(regfile_1_operand1), .Operand2(regfile_1_operand2));  // open: WriteData, CLK, ReadAddress1, WriteAddress, ReadAddress2
  ALU alu_1 (
    .Operand1(regfile_1_operand1), .Operand2(regfile_1_operand2));  // open: ALU_Function, CarryFlag, ALU_Output, ZeroFlag
endmodule

module RegFile (
  input  [15:0] WriteData,
  input  CLK,
  input  [3:0] ReadAddress1,
  input  [3:0] WriteAddress,
  input  [3:0] ReadAddress2,
  output [15:0] Operand1,
  output [15:0] Operand2
);

  wire decoder_1_out0, decoder_1_out1, decoder_1_out2, decoder_1_out3, decoder_1_out4, decoder_1_out5,
       decoder_1_out6, decoder_1_out7, decoder_1_out8, decoder_1_out9, decoder_1_out10, decoder_1_out11,
       decoder_1_out12, decoder_1_out13, decoder_1_out14, decoder_1_out15;
  wire [15:0] register_1_q, register_2_q, register_3_q, register_4_q, register_5_q, register_6_q,
       register_7_q, register_8_q, register_9_q, register_10_q, register_11_q, register_12_q, register_13_q,
       register_14_q, register_15_q, register_16_q;

  Decoder #(.select(4)) decoder_1 (
    .out0(decoder_1_out0), .out1(decoder_1_out1), .out2(decoder_1_out2), .out3(decoder_1_out3),
    .out4(decoder_1_out4), .out5(decoder_1_out5), .out6(decoder_1_out6), .out7(decoder_1_out7),
    .out8(decoder_1_out8), .out9(decoder_1_out9), .out10(decoder_1_out10), .out11(decoder_1_out11),
    .out12(decoder_1_out12), .out13(decoder_1_out13), .out14(decoder_1_out14), .out15(decoder_1_out15),
    .sel(WriteAddress));  // open: en
  Register #(.width(16)) register_1 (.D(WriteData), .en(decoder_1_out0), .Q(register_1_q), .clk(CLK));  // open: clr
  Register #(.width(16)) register_2 (.D(WriteData), .en(decoder_1_out1), .Q(register_2_q), .clk(CLK));  // open: clr
  Register #(.width(16)) register_3 (.D(WriteData), .en(decoder_1_out2), .Q(register_3_q), .clk(CLK));  // open: clr
  Register #(.width(16)) register_4 (.D(WriteData), .en(decoder_1_out3), .Q(register_4_q), .clk(CLK));  // open: clr
  Register #(.width(16)) register_5 (.D(WriteData), .en(decoder_1_out4), .Q(register_5_q), .clk(CLK));  // open: clr
  Register #(.width(16)) register_6 (.D(WriteData), .en(decoder_1_out5), .Q(register_6_q), .clk(CLK));  // open: clr
  Register #(.width(16)) register_7 (.D(WriteData), .en(decoder_1_out6), .Q(register_7_q), .clk(CLK));  // open: clr
  Register #(.width(16)) register_8 (.D(WriteData), .en(decoder_1_out7), .Q(register_8_q), .clk(CLK));  // open: clr
  Register #(.width(16)) register_9 (.D(WriteData), .en(decoder_1_out8), .Q(register_9_q), .clk(CLK));  // open: clr
  Register #(.width(16)) register_10 (.D(WriteData), .en(decoder_1_out9), .Q(register_10_q), .clk(CLK));  // open: clr
  Register #(.width(16)) register_11 (.D(WriteData), .en(decoder_1_out10), .Q(register_11_q), .clk(CLK));  // open: clr
  Register #(.width(16)) register_12 (.D(WriteData), .en(decoder_1_out11), .Q(register_12_q), .clk(CLK));  // open: clr
  Register #(.width(16)) register_13 (.D(WriteData), .en(decoder_1_out12), .Q(register_13_q), .clk(CLK));  // open: clr
  Register #(.width(16)) register_14 (.D(WriteData), .en(decoder_1_out13), .Q(register_14_q), .clk(CLK));  // open: clr
  Register #(.width(16)) register_15 (.D(WriteData), .en(decoder_1_out14), .Q(register_15_q), .clk(CLK));  // open: clr
  Register #(.width(16)) register_16 (.D(WriteData), .en(decoder_1_out15), .Q(register_16_q), .clk(CLK));  // open: clr
  Multiplexer #(.select(4), .width(16)) multiplexer_1 (
    .in0(register_1_q), .in1(register_2_q), .in2(register_3_q), .in3(register_4_q), .in4(register_5_q),
    .in5(register_6_q), .in6(register_7_q), .in7(register_8_q), .in8(register_9_q), .in9(register_10_q),
    .in10(register_11_q), .in11(register_12_q), .in12(register_13_q), .in13(register_14_q),
    .in14(register_15_q), .in15(register_16_q), .out(Operand1), .sel(ReadAddress1));
  Multiplexer #(.select(4), .width(16)) multiplexer_2 (
    .in0(register_1_q), .in1(register_2_q), .in2(register_3_q), .in3(register_4_q), .in4(register_5_q),
    .in5(register_6_q), .in6(register_7_q), .in7(register_8_q), .in8(register_9_q), .in9(register_10_q),
    .in10(register_11_q), .in11(register_12_q), .in12(register_13_q), .in13(register_14_q),
    .in14(register_15_q), .in15(register_16_q), .out(Operand2), .sel(ReadAddress2));
endmodule

module ALU (
  input  [3:0] ALU_Function,
  input  [15:0] Operand1,
  input  [15:0] Operand2,
  output CarryFlag,
  output [15:0] ALU_Output,
  output ZeroFlag
);

  wire arithmeticunit_1_carryout;
  wire [15:0] arithmeticunit_1_arithmetic_out, logicalunit_1_logicalout;

  and and_1 (CarryFlag, ~ALU_Function[3], arithmeticunit_1_carryout);  // AND_Gate
  ArithmeticUnit arithmeticunit_1 (
    .ALU_Function(ALU_Function), .Operand1(Operand1), .Operand2(Operand2),
    .Arithmetic_Out(arithmeticunit_1_arithmetic_out), .CarryOut(arithmeticunit_1_carryout));
  LogicalUnit logicalunit_1 (
    .ALU_Function(ALU_Function), .Operand1(Operand1), .Operand2(Operand2),
    .LogicalOut(logicalunit_1_logicalout));
  Multiplexer #(.width(16)) multiplexer_1 (
    .in0(arithmeticunit_1_arithmetic_out), .in1(logicalunit_1_logicalout), .out(ALU_Output),
    .sel(ALU_Function[3]));
  nor nor_1 (ZeroFlag, ALU_Output[0], ALU_Output[1], ALU_Output[2], ALU_Output[3], ALU_Output[4], ALU_Output[5], ALU_Output[6], ALU_Output[7], ALU_Output[9], ALU_Output[10], ALU_Output[11], ALU_Output[12], ALU_Output[13], ALU_Output[14], ALU_Output[15], ALU_Output[8]);
endmodule

module LogicalUnit (
  input  [3:0] ALU_Function,
  input  [15:0] Operand1,
  input  [15:0] Operand2,
  output [15:0] LogicalOut
);

  wire [15:0] and_1_out, bit_extender_1_out, multiplexer_1_out, or_1_out, xor_1_out;

  assign and_1_out = Operand1 & Operand2;  // AND_Gate and_1, 16 bits wide
  assign or_1_out = Operand1 | Operand2;  // OR_Gate or_1, 16 bits wide
  assign xor_1_out = Operand1 ^ Operand2;  // XOR_Gate xor_1, 16 bits wide
  Multiplexer #(.select(2), .width(16)) multiplexer_1 (
    .in0(Operand1), .in1(and_1_out), .in2(or_1_out), .in3(xor_1_out), .out(multiplexer_1_out),
    .sel(ALU_Function[1:0]));
  assign bit_extender_1_out = {{15{ALU_Function[2]}}, ALU_Function[2]};  // Bit_Extender bit_extender_1
  assign LogicalOut = bit_extender_1_out ^ multiplexer_1_out;  // XOR_Gate xor_2, 16 bits wide

  // Other names for the same wires on the sheet: LogicalFunction[1:0] = ALU_Function[1:0]; Inverted = ALU_Function[2]
endmodule

module ArithmeticUnit (
  input  [3:0] ALU_Function,
  input  [15:0] Operand1,
  input  [15:0] Operand2,
  output [15:0] Arithmetic_Out,
  output CarryOut
);

  wire adder_1_cout, subtractor_1_bout;
  wire [3:0] bit_extender_1_out;
  wire [15:0] adder_1_out, shifter_1_out, shifter_2_out, subtractor_1_out;

  Bit_Extender #(.in_width(16), .out_width(4)) bit_extender_1 (.in(Operand2), .out(bit_extender_1_out));
  Adder #(.width(16)) adder_1 (.a(Operand1), .b(Operand2), .out(adder_1_out), .cout(adder_1_cout));  // open: cin
  Subtractor #(.width(16)) subtractor_1 (
    .a(Operand1), .b(Operand2), .out(subtractor_1_out), .bout(subtractor_1_bout));  // open: bin
  Shifter #(.width(16)) shifter_1 (.in(Operand1), .\dist (bit_extender_1_out), .out(shifter_1_out));
  Shifter #(.shift("lr"), .width(16)) shifter_2 (.in(Operand1), .\dist (bit_extender_1_out), .out(shifter_2_out));
  Multiplexer #(.select(3), .width(16)) multiplexer_1 (
    .in0(adder_1_out), .in1(subtractor_1_out), .in2(shifter_1_out), .in3(shifter_2_out), .in4({16{1'b0}}),
    .in5({16{1'b0}}), .in6({16{1'b0}}), .in7({16{1'b0}}), .out(Arithmetic_Out), .sel(ALU_Function[2:0]));
  Multiplexer #(.select(3)) multiplexer_2 (
    .in0(adder_1_cout), .in1(subtractor_1_bout), .in2(1'b0), .in3(1'b0), .in4(1'b0), .in5(1'b0), .in6(1'b0),
    .in7(1'b0), .out(CarryOut), .sel(ALU_Function[2:0]));

  // Other names for the same wires on the sheet: MathFunction[2:0] = ALU_Function[2:0]
endmodule
